// Logisim project MaszynaW.circ as structural Verilog: 5 circuits, main circuit main
module main (
  input  BTN_CLK,
  input  [15:0] in_2,
  input  Hand_CPU,
  output [4:0] out_4,
  output [4:0] out_5,
  output [4:0] out_6,
  output [7:0] out_7,
  output [7:0] out_8,
  output [2:0] out_9,
  output [4:0] out_10,
  output [7:0] out_11
);

  wire button_1_out, clk, clock_1_out, czyt, dod, il, multiplexer_1_out, ode, pisz, przep, rst, stp, wea,
       \weak , wei, weja, wel, wes, wyad, wyak, wyl, wys, z, zak;
  wire [15:0] ctrl;

  Button button_1 (.out(button_1_out));
  Clock clock_1 (.out(clock_1_out));
  Button button_2 (.out(rst));
  Pc pc_1 (.clk(clk), .rst(rst), .wyjl(out_4), .wejl(out_4), .wyl(wyl), .wel(wel), .il(il), .L(out_5));
  Multiplexer #(.enable("false")) multiplexer_1 (
    .in0(button_1_out), .in1(clock_1_out), .out(multiplexer_1_out), .sel(BTN_CLK));
  and and_1 (clk, multiplexer_1_out, ~stp);  // AND_Gate
  LED STOP (.in(stp));
  Inst inst_1 (
    .wyad(wyad), .weji(out_11), .minus(z), .wei(wei), .zero(zak), .clk(clk), .rst(rst), .ctrl(ctrl),
    .addr(out_10), .wyjad(out_4), .inst(out_9), .stp(stp));
  Multiplexer #(.width(16), .enable("false")) multiplexer_2 (
    .in0(in_2), .in1(ctrl),
    .out({il, wyl, wel, wea, wei, wyad, \weak , dod, ode, przep, weja, wyak, wes, wys, czyt, pisz}),
    .sel(Hand_CPU));
  JAL jal_1 (
    .\weak (\weak ), .wejja(out_11), .wyak(wyak), .przep(przep), .ode(ode), .dod(dod), .clk(clk), .rst(rst),
    .wyja(out_11), .weja(weja), .ak(out_7), .minus(z), .zero(zak));
  Mem mem_1 (
    .weja(out_4), .wea(wea), .pisz(pisz), .czyt(czyt), .wejs(out_11), .wes(wes), .wys(wys), .wyjs(out_11),
    .rst(rst), .clk(clk), .A(out_6), .S(out_8));

  // Notes on the sheet:
  //   MASZYNA W
endmodule

module Mem (
  input  [4:0] weja,
  input  wea,
  input  rst,
  input  pisz,
  input  czyt,
  input  [7:0] wejs,
  input  clk,
  input  wys,
  input  wes,
  output [4:0] A,
  output [7:0] S,
  output [7:0] wyjs
);

  wire or_1_out, or_2_out;
  wire [4:0] multiplexer_1_out;
  wire [7:0] multiplexer_2_out, ram_1_data;

  Multiplexer #(.width(5), .enable("false")) multiplexer_1 (
    .in1(weja), .out(multiplexer_1_out), .sel(wea));  // open: in0
  Register #(.width(5), .trigger("high")) u_A (.D(multiplexer_1_out), .Q(A), .clk(clk), .clr(rst));  // open: en
  // NOT_Gate not_1 has open pins: in=clk, out=open
  Multiplexer #(.width(8), .enable("false")) multiplexer_2 (
    .in0(ram_1_data), .in1(wejs), .out(multiplexer_2_out), .sel(wes));
  or or_1 (or_1_out, czyt, clk);
  or or_2 (or_2_out, pisz, czyt);
  Register #(.trigger("high")) u_S (.D(multiplexer_2_out), .Q(S), .clk(or_1_out), .clr(rst));  // open: en
  RAM #(.addrWidth(5), .bus("separate")) ram_1 (
    .addr(A), .din(S), .data(ram_1_data), .str(pisz), .sel(1'b1), .clk(or_2_out), .ld(czyt));  // open: clr
  Multiplexer #(.width(8), .enable("false")) multiplexer_3 (.in1(S), .out(wyjs), .sel(wys));  // open: in0
endmodule

module Pc (
  input  wel,
  input  [4:0] wejl,
  input  il,
  input  clk,
  input  rst,
  input  wyl,
  output [4:0] L,
  output [4:0] wyjl
);

  Multiplexer #(.width(5), .enable("false")) multiplexer_1 (.in1(L), .out(wyjl), .sel(wyl));  // open: in0
  Counter #(.width(5), .max('h1f)) counter_1 (
    .load(wel), .D(wejl), .count(il), .Q(L), .clk(clk), .clr(rst));  // open: carry
endmodule

module JAL (
  input  \weak ,
  input  [7:0] wejja,
  input  weja,
  input  wyak,
  input  przep,
  input  ode,
  input  dod,
  input  clk,
  input  rst,
  output zero,
  output minus,
  output [7:0] ak,
  output [7:0] wyja
);

  wire [7:0] adder_1_out, multiplexer_1_out, multiplexer_2_out, subtractor_1_out;

  Multiplexer #(.width(8), .enable("false")) multiplexer_1 (
    .in1(wejja), .out(multiplexer_1_out), .sel(weja));  // open: in0
  Adder adder_1 (.a(ak), .b(multiplexer_1_out), .out(adder_1_out));  // open: cin, cout
  Subtractor subtractor_1 (.a(ak), .b(multiplexer_1_out), .out(subtractor_1_out));  // open: bin, bout
  Multiplexer #(.select(2), .width(8), .enable("false")) multiplexer_2 (
    .in0(adder_1_out), .in1(subtractor_1_out), .in2(multiplexer_1_out), .out(multiplexer_2_out),
    .sel({przep, ode}));  // open: in3
  Register u_AK (.D(multiplexer_2_out), .en(\weak ), .Q(ak), .clk(clk), .clr(rst));
  Multiplexer #(.width(8), .enable("false")) multiplexer_3 (.in1(ak), .out(wyja), .sel(wyak));  // open: in0
  nor nor_1 (zero, ak[0], ak[1], ak[2], ak[3], ak[4], ak[5], ak[6], ak[7]);

  assign minus = ak[7];
  // also tied to GND on the sheet: dod
endmodule

module Inst (
  input  wyad,
  input  [7:0] weji,
  input  minus,
  input  wei,
  input  zero,
  input  clk,
  input  rst,
  output [15:0] ctrl,
  output [4:0] addr,
  output [4:0] wyjad,
  output [2:0] inst,
  output stp
);

  wire nor_1_out, or_1_out, or_2_out;
  wire [1:0] counter_1_q;
  wire [2:2] multiplexer_3_out;
  wire [7:0] multiplexer_1_out;

  Multiplexer #(.width(8), .enable("false")) multiplexer_1 (
    .in1(weji), .out(multiplexer_1_out), .sel(wei));  // open: in0
  or or_1 (or_1_out, rst, nor_1_out);
  Register register_1 (.D(multiplexer_1_out), .Q({inst, addr}), .clk(clk), .clr(or_1_out));  // open: en
  Counter #(.width(2), .max('h3), .trigger("falling")) counter_1 (
    .load(1'b0), .count(1'b1), .Q(counter_1_q), .clk(clk), .clr(or_2_out));  // open: D, carry
  or or_2 (or_2_out, rst, nor_1_out);
  Multiplexer #(.width(5), .enable("false")) multiplexer_2 (.in1(addr), .out(wyjad), .sel(wyad));  // open: in0
  Multiplexer #(.enable("false")) multiplexer_3 (.in0(minus), .in1(zero), .out(multiplexer_3_out[2]), .sel(inst[0]));
  ROM #(.addrWidth(6), .dataWidth(16)) rom_1 (
    .addr({inst, multiplexer_3_out[2], counter_1_q}), .data(ctrl), .sel(1'b1));
  nor nor_1 (nor_1_out, ctrl[0], ctrl[1], ctrl[2], ctrl[3], ctrl[4], ctrl[5], ctrl[6], ctrl[7], ctrl[8], ctrl[9], ctrl[10], ctrl[11], ctrl[12], ctrl[13], ctrl[14], ctrl[15]);
  and and_1 (stp, ctrl[0], ctrl[1], ctrl[2], ctrl[3], ctrl[4], ctrl[5], ctrl[6], ctrl[7], ctrl[8], ctrl[9], ctrl[10], ctrl[11], ctrl[12], ctrl[13], ctrl[14], ctrl[15]);

  // Notes on the sheet:
  //   contents of rom_1 (hex, n*v repeats v):
  //   8806 ffff 0 0 8806 ffff 0 0 8806 1400 5326 0 8806 1400 5326 0 8806 1400 52a6 0 8806 1400 52a6 0 8806
  //   1400 5266 0 8806 1400 5266 0 8806 1418 5001 0 8806 1418 5001 0 8806 3400 0 0 8806 3400 0 0 8806 5000
  //   0 0 8806 3400 0 0 8806 5000 0 0 8806 3400
endmodule
